# Fritzing sketch ESP01 Challenge - Fritzing (saved by Fritzing 0.9.9b)

parts:
  U1 = ESP8266 ESP-01 Upgraded WiFi Module [part_number=ESP8266]
  Mod1 = Amica NodeMCU DEVKIT 1.0
  VCC1 = Battery
  M1 = RioRand LM2596

nets:
  N1: U1.RXD, Mod1.pin8
  N2: U1.VCC, Mod1.pin1, Mod1.pin_10, M1.Pin_3
  N3: U1.TXD, Mod1.pin_11
  N4: Mod1.pin2, Mod1.pin_9, M1.Pin_4
  N5: VCC1.-, M1.Pin_2
  N6: VCC1.+, M1.Pin_1

custom parts:
  ESP8266 ESP-01 Upgraded WiFi Module: Upgraded Version ESP-01,all Flash are upgraded to 1M byte.Also support Cloud service remote transmission.
  Battery: Your standard 2x 18650 battery pack (7,4 Volts)
